# Fritzing sketch AS5311MagnSide3Vcap1 (saved by Fritzing 1.0.6)
circuit board: 5.99999cm x 2.65001cm
breadboards: 1

parts:
  IC1 = TSSOP20 [chip_label=AS5311 package=TSSOP]
  C1 = Ceramic Capacitor [capacitance=200nF voltage=10V package="100 mil [THT, multilayer]"]
  C2 = Electrolytic Capacitor [capacitance=10µF voltage=10V package="100 mil [THT, electrolytic]"]
  J1 = female pin header, 4 pins [form="♀ (female)"]

nets:
  N1: IC1.4, J1.pin2
  N2: IC1.5, J1.pin1
  GND: IC1.8, IC1.9, IC1.14, C1.1, C2.-, J1.pin3
  N3: IC1.18, C2.+
  5V: IC1.19, C1.0, J1.pin4

notes:
  saved 21dec2025
  5V
  W. Berggren dec2025
  B
  GND
  A
  10uF
  200nF
  CSn
  prog
  3.3V
