# Fritzing sketch AS5311small (saved by Fritzing 1.0.6)
circuit board: 6cm x 2.6cm
breadboards: 1

parts:
  IC1 = TSSOP20 [chip_label=AS5311 package=TSSOP]
  C2 = Electrolytic Capacitor [capacitance=10µF voltage=35V package="100 mil [THT, electrolytic]"]
  C1 = Ceramic Capacitor [capacitance=100nF voltage=35V package="100 mil [THT, multilayer]"]
  J1 = female pin header, 4 pins [form="♀ (female)"]

nets:
  N1: IC1.4, J1.pin1
  N2: IC1.5, J1.pin2
  N3: IC1.8, IC1.9, IC1.14, C2.-, C1.1, J1.pin4
  N4: IC1.18, C2.+
  N5: IC1.19, C1.0, J1.pin3

notes:
  A
  B
  GND
  5V
  Berggren jan 2026
